// Logisim project multipleksor.circ as structural Verilog: 1 circuit, main circuit main
module main (
  input  A0,
  input  A1,
  input  A2,
  input  M0,
  input  M2,
  input  M1,
  input  M3,
  input  M4,
  input  M6,
  input  M5,
  input  M7,
  output Out
);

  wire _1_2_out, _1_3_out, _1_4_out, _1_5_out, _1_6_out, _1_7_out, _1_8_out, _1_9_out, _1_10_out, _1_11_out,
       _1_12_out, _1_13_out, _1_14_out, _1_15_out, _1_17_out, _1_18_out, _1_19_out, _1_20_out, _1_out,
       _2_2_out, _2_3_out, _2_4_out, _2_5_out, _2_6_out, _2_7_out, _2_8_out, _2_9_out, _2_10_out, _2_11_out,
       _2_12_out, _2_13_out, _2_14_out, _2_15_out, _2_16_out, _2_17_out, _2_out;

  not _1 (_1_out, A0);
  not _1_2 (_1_2_out, A1);
  not _1_3 (_1_3_out, A2);
  nand _2 (_2_out, A2, A1, A0);
  nand _2_2 (_2_2_out, A2, _1_2_out, A0);
  nand _2_3 (_2_3_out, A2, A1, _1_out);
  nand _2_4 (_2_4_out, A2, _1_2_out, _1_out);
  nand _2_5 (_2_5_out, _1_3_out, A1, A0);
  nand _2_6 (_2_6_out, _1_3_out, _1_2_out, A0);
  nand _2_7 (_2_7_out, _1_3_out, A1, _1_out);
  nand _2_8 (_2_8_out, _1_3_out, _1_2_out, _1_out);
  not _1_4 (_1_4_out, _2_out);
  not _1_5 (_1_5_out, _2_2_out);
  not _1_6 (_1_6_out, _2_3_out);
  not _1_7 (_1_7_out, _2_4_out);
  not _1_8 (_1_8_out, _2_5_out);
  not _1_9 (_1_9_out, _2_6_out);
  not _1_10 (_1_10_out, _2_7_out);
  not _1_11 (_1_11_out, _2_8_out);
  nand _2_9 (_2_9_out, _1_11_out, M0);
  not _1_12 (_1_12_out, _2_9_out);
  nand _2_10 (_2_10_out, _1_10_out, M2);
  not _1_13 (_1_13_out, _2_10_out);
  nand _2_11 (_2_11_out, _1_9_out, M1);
  not _1_14 (_1_14_out, _2_11_out);
  nand _2_12 (_2_12_out, _1_8_out, M3);
  not _1_15 (_1_15_out, _2_12_out);
  nor _2_13 (_2_13_out, _1_12_out, _1_13_out, _1_14_out, _1_15_out, _1_17_out, _1_18_out, _1_19_out, _1_20_out);
  not _1_16 (Out, _2_13_out);
  nand _2_14 (_2_14_out, _1_7_out, M4);
  nand _2_15 (_2_15_out, _1_6_out, M6);
  not _1_17 (_1_17_out, _2_14_out);
  not _1_18 (_1_18_out, _2_15_out);
  nand _2_16 (_2_16_out, _1_5_out, M5);
  not _1_19 (_1_19_out, _2_16_out);
  nand _2_17 (_2_17_out, _1_4_out, M7);
  not _1_20 (_1_20_out, _2_17_out);

  // Notes on the sheet:
  //   Едакина Мария Б01-404
  //   8-входовой мультиплексор
endmodule
